# Fritzing sketch toscolight (saved by Fritzing 0.9.1b)
breadboards: 1

parts:
  Componente1 = Arduino Leonardo (Rev3b)
  R1 = Resistor [tolerance=±5% resistance=470 package="0805 [SMD]"]
  C1 = Capacitor Polarized [package=cpol-radial-1000uf-25v]
  C2 = Capacitor Polarized [package=cpol-radial-1000uf-25v]
  NEOPIXEL1 = Neopixel Strip -- White (60/m)
  NEOPIXEL2 = Neopixel Strip -- White (60/m)

nets:
  N1: Componente1.D6_PWM/A7, R1.Pin_0
  5V: Componente1.5V, C1.+, NEOPIXEL1.+5V
  GND: Componente1.GND, C1.-, C2.-, NEOPIXEL1.GND, NEOPIXEL2.GND
  N2: R1.Pin_1, NEOPIXEL1.DI
  N3: C2.+, NEOPIXEL2.+5V
  N4: NEOPIXEL1.DO, NEOPIXEL2.DI

notes:
  - DC 5V 8A
  +
  96 LEDs
  6.3V 1000uF

custom parts:
  Neopixel Strip -- White (60/m): Neopixel Strip, White, 60 pixels per meter.
